# Fritzing sketch streamdeck (saved by Fritzing 0.9.10b)

parts:
  /F13 = Square Pushbutton
  /F14 = Square Pushbutton
  tglDEAFEN/F15 = Square Pushbutton
  tglSCREENSHARE/F17 = Square Pushbutton
  tglMUTE/F18 = Square Pushbutton
  openCalculator/F16 = Square Pushbutton
  Anlage_Ein = LTE-302 [package=lte-302]
  Eingabe = LTE-302 [package=lte-302]
  RP2040_Microcontroller = Raspberry Pi Pico H
  Volume_Control = KY-040 Rotary encoder [package=THT]

nets (from the breadboard view):
  N1: /F13.leg0, /F14.leg0, tglDEAFEN/F15.leg0, RP2040_Microcontroller.GP14
  N2: /F13.leg1, openCalculator/F16.leg1, RP2040_Microcontroller.GP8
  N3: /F14.leg1, tglSCREENSHARE/F17.leg1, RP2040_Microcontroller.GP7
  N4: tglDEAFEN/F15.leg1, tglMUTE/F18.leg1, RP2040_Microcontroller.GP6
  N5: tglSCREENSHARE/F17.leg0, tglMUTE/F18.leg0, openCalculator/F16.leg0, RP2040_Microcontroller.GP15
  N6: Anlage_Ein.A, RP2040_Microcontroller.VBUS
  GND: Anlage_Ein.C, Eingabe.C, RP2040_Microcontroller.GND, Volume_Control.GND
  N7: Eingabe.A, RP2040_Microcontroller.GP9
  3V3: RP2040_Microcontroller.3V3, Volume_Control.Vcc
  N8: RP2040_Microcontroller.GP12, Volume_Control.SW
  N9: RP2040_Microcontroller.GP11, Volume_Control.DT
  N10: RP2040_Microcontroller.GP10, Volume_Control.CLK

custom parts:
  Raspberry Pi Pico H: Raspberry Pi Pico H. Based around the RP2040 microcontroller the Pico H is a low cost microcontroller device bringing Raspberry Pi quality, cost, and easy of use to the microcontroller space.
  KY-040 Rotary encoder: KY-040 Rotary Encoder with switch on breakout borad from AZ Delivery
