# Fritzing sketch Tastatur (saved by Fritzing 0.9.10b)

parts:
  openCalculator/F13 = Square Pushbutton
  disconnectChannel/F14 = Square Pushbutton
  tglDEAFEN/F15 = Square Pushbutton
  tglSCREENSHARE/F17 = Square Pushbutton
  tglMUTE/F18 = Square Pushbutton
  openSoundboard/F16 = Square Pushbutton
  Bauteil3 = Arduino Micro (Rev3)
  Anlage_Ein = LTE-302 [package=lte-302]
  Eingabe = LTE-302 [package=lte-302]

nets:
  N1: openCalculator/F13.leg0, disconnectChannel/F14.leg0, tglDEAFEN/F15.leg0, Bauteil3.D8_PWM/A8
  N2: openCalculator/F13.leg1, openSoundboard/F16.leg1, Bauteil3.D10_PWM/A10
  N3: disconnectChannel/F14.leg1, tglSCREENSHARE/F17.leg1, Bauteil3.D11_PWM
  N4: tglDEAFEN/F15.leg1, tglMUTE/F18.leg1, Bauteil3.D12_PWM/A11
  N5: tglSCREENSHARE/F17.leg0, tglMUTE/F18.leg0, openSoundboard/F16.leg0, Bauteil3.D7
  N6: Bauteil3.GND, Anlage_Ein.C, Eingabe.C
  N7: Bauteil3.D3/SCL, Anlage_Ein.A
  N8: Bauteil3.D5_PWM, Eingabe.A
